# Fritzing sketch breadboard-wireup (saved by Fritzing 1.0.5)
breadboards: 3

parts:
  S1 = Pushbutton [package="[THT]"]
  S2 = Pushbutton [package="[THT]"]
  S3 = Pushbutton [package="[THT]"]
  Mod1 = Amica NodeMCU DEVKIT 1.0
  S4 = Pushbutton [package="[THT]"]
  J1 = Piezo Speaker
  J2 = Piezo Speaker
  R1 = Resistor [tolerance=±5% resistance=680 package="0603 [SMD]"]
  R2 = Resistor [tolerance=±5% resistance=680 package="0603 [SMD]"]
  R3 = Resistor [tolerance=±5% resistance=680 package="0603 [SMD]"]
  R5 = Resistor [tolerance=±5% resistance=680 package="0603 [SMD]"]
  R6 = Resistor [tolerance=±5% resistance=680 package="0603 [SMD]"]
  R7 = Resistor [tolerance=±5% resistance=680 package="0603 [SMD]"]
  U1 = POT [knob_status=50% power=0.5W package=pot_alpha_rv16af-20]

nets:
  N1: S1.Pin_1, S1.Pin_2, S2.Pin_1, S2.Pin_2, S3.Pin_1, S3.Pin_2, Mod1.pin2, Mod1.pin_9, Mod1.pin_25, Mod1.pin_29, S4.Pin_1, S4.Pin_2, J1.pin1, J2.pin1, U1.A
  N2: S1.Pin_3, S1.Pin_4, Mod1.pin_15, R3.Pin_1
  N3: S2.Pin_3, S2.Pin_4, Mod1.pin8, R5.Pin_1
  N4: S3.Pin_3, S3.Pin_4, Mod1.pin6, R7.Pin_1
  N5: Mod1.pin1, Mod1.pin_10, Mod1.pin_26, R3.Pin_0, R5.Pin_0, R6.Pin_0, R7.Pin_0, U1.E
  N6: Mod1.pin7, S4.Pin_3, S4.Pin_4, R6.Pin_1
  N7: Mod1.pin_13, R2.Pin_1
  N8: Mod1.pin_14, R1.Pin_1
  N9: Mod1.pin_16, U1.S
  N10: J1.pin2, R1.Pin_0
  N11: J2.pin2, R2.Pin_0
