# Fritzing sketch fritzing-breadboard (saved by Fritzing 1.0.5)
breadboards: 4

parts:
  S1 = Pushbutton [package="[THT]"]
  S2 = Pushbutton [package="[THT]"]
  S3 = Pushbutton [package="[THT]"]
  Mod1 = Amica NodeMCU DEVKIT 1.0
  S4 = Pushbutton [package="[THT]"]
  J1 = Piezo Speaker
  J2 = Piezo Speaker
  R1 = Resistor [tolerance=±5% resistance=680 package="0603 [SMD]"]
  R2 = Resistor [tolerance=±5% resistance=680 package="0603 [SMD]"]
  R3 = Resistor [tolerance=±5% resistance=680 package="0603 [SMD]"]
  R5 = Resistor [tolerance=±5% resistance=680 package="0603 [SMD]"]
  R6 = Resistor [tolerance=±5% resistance=680 package="0603 [SMD]"]
  R7 = Resistor [tolerance=±5% resistance=680 package="0603 [SMD]"]
  U1 = POT [knob_status=50% power=0.5W package=pot_alpha_rv16af-20]
  U2 = WS2812 RGB LED strip
  C1 = Electrolytic Capacitor [capacitance=1µF voltage=35V package="100 mil [THT, electrolytic]"]
  R8 = Resistor [tolerance=±5% resistance=680 package="0603 [SMD]"]

nets:
  N1: S1.Pin_1, S1.Pin_2, S2.Pin_1, S2.Pin_2, S3.Pin_1, S3.Pin_2, Mod1.pin2, Mod1.pin_9, Mod1.pin_25, Mod1.pin_29, S4.Pin_1, S4.Pin_2, J1.pin1, J2.pin1, U1.A, U2.GND, C1.-
  N2: S1.Pin_3, S1.Pin_4, Mod1.pin_15, R3.Pin_1
  N3: S2.Pin_3, S2.Pin_4, Mod1.pin8, R5.Pin_1
  N4: S3.Pin_3, S3.Pin_4, Mod1.pin6, R7.Pin_1
  N5: Mod1.pin1, Mod1.pin_10, Mod1.pin_26, R3.Pin_0, R5.Pin_0, R6.Pin_0, R7.Pin_0, U1.E
  N6: Mod1.pin7, S4.Pin_3, S4.Pin_4, R6.Pin_1
  N7: Mod1.pin_11, R8.Pin_0
  N8: Mod1.pin_13, R2.Pin_1
  N9: Mod1.pin_14, R1.Pin_1
  N10: Mod1.pin_16, U1.S
  N11: Mod1.pin_30, U2.VCC, C1.+
  N12: J1.pin2, R1.Pin_0
  N13: J2.pin2, R2.Pin_0
  N14: U2.DOUT, R8.Pin_1

custom parts:
  WS2812 RGB LED strip: WS2812 strip
